// Logisim project proj1.circ as structural Verilog: 13 circuits, main circuit main
module main (
);

  wire clock_1_out, days_1_carry, hours_12_1_carry, months_1_a, months_1_b, months_1_carry, p, undriven,
       undriven_2;
  wire [3:0] d0, d1, h0, h1, m0, m1, n0, n1, s0, s1, y0, y1, y2, y3;

  Hex_Digit_Display hex_digit_display_1 (.value(y2));  // open: dp
  Hex_Digit_Display hex_digit_display_2 (.value(y3));  // open: dp
  Hex_Digit_Display hex_digit_display_3 ();  // open: value, dp
  Hex_Digit_Display hex_digit_display_4 (.value(y0));  // open: dp
  Hex_Digit_Display hex_digit_display_5 (.value(y1));  // open: dp
  Hex_Digit_Display hex_digit_display_6 ();  // open: value, dp
  Button button_1 ();  // open: out
  seconds seconds_1 (.OUTPUT_0(s0), .OUTPUT_1(s1), .CARRY(undriven), .CLK(clock_1_out));
  Clock clock_1 (.out(clock_1_out));
  Hex_Digit_Display hex_digit_display_7 (.value(n1));  // open: dp
  Hex_Digit_Display hex_digit_display_8 ();  // open: value, dp
  Hex_Digit_Display hex_digit_display_9 ();  // open: value, dp
  minutes minutes_1 (.CLK(undriven), .CARRY(undriven_2), .OUTPUT_0(m0), .OUTPUT_1(m1));
  Hex_Digit_Display hex_digit_display_10 (.value(d1));  // open: dp
  Hex_Digit_Display hex_digit_display_11 (.value(n0));  // open: dp
  Hex_Digit_Display hex_digit_display_12 (.value(d0));  // open: dp
  hours_12 hours_12_1 (
    .OUTPUT_1(h1), .OUTPUT_0(h0), .PERIOD(p), .CLK(undriven_2), .CARRY(hours_12_1_carry));  // open: RESET
  Hex_Digit_Display hex_digit_display_13 (.value(h0));  // open: dp
  Hex_Digit_Display hex_digit_display_14 (.value(h1));  // open: dp
  days days_1 (
    .OUTPUT_1(d1), .OUTPUT_0(d0), .A(months_1_a), .B(months_1_b), .CARRY(days_1_carry), .CLK(hours_12_1_carry));
  Hex_Digit_Display hex_digit_display_15 (.value(m1));  // open: dp
  Hex_Digit_Display hex_digit_display_16 (.value(m0));  // open: dp
  months months_1 (
    .CLK(days_1_carry), .CARRY(months_1_carry), .OUTPUT_1(n1), .OUTPUT_0(n0), .a(months_1_a), .b(months_1_b));  // open: RESET
  Hex_Digit_Display hex_digit_display_17 (.value(s1));  // open: dp
  years years_1 (.OUTPUT_0(y0), .OUTPUT_1(y1), .OUTPUT_2(y2), .OUTPUT_3(y3), .CLK(months_1_carry));  // open: CARRY
  LED AM (.in(p));
  LED #(.active("false")) PM (.in(p));
  Hex_Digit_Display hex_digit_display_18 (.value(s0));  // open: dp
endmodule

module seconds (
  input  CARRY,
  input  CLK,
  output [3:0] OUTPUT_0,
  output [3:0] OUTPUT_1
);

  wire counter_2_carry;

  Counter #(.width(4), .max('h6)) counter_1 (
    .Q(OUTPUT_1), .carry(CARRY), .clk(counter_2_carry), .clr(CARRY));  // open: load, D, count
  Counter #(.width(4), .max('ha)) counter_2 (
    .Q(OUTPUT_0), .carry(counter_2_carry), .clk(CLK), .clr(counter_2_carry));  // open: load, D, count
endmodule

module minutes (
  input  CARRY,
  input  CLK,
  output [3:0] OUTPUT_0,
  output [3:0] OUTPUT_1
);

  wire counter_2_carry;

  Counter #(.width(4), .max('h6)) counter_1 (
    .Q(OUTPUT_1), .carry(CARRY), .clk(counter_2_carry), .clr(CARRY));  // open: load, D, count
  Counter #(.width(4), .max('ha)) counter_2 (
    .Q(OUTPUT_0), .carry(counter_2_carry), .clk(CLK), .clr(counter_2_carry));  // open: load, D, count
endmodule

module hours_12 (
  input  CLK,
  input  RESET,
  output [3:0] OUTPUT_1,
  output [3:0] OUTPUT_0,
  output CARRY,
  output PERIOD
);

  wire and_1_out, counter_1_carry, counter_4_carry, or_1_out, or_2_out, or_3_out, t_ff_1_q, t_ff_1_qn;
  wire [3:0] adder_1_out, counter_1_q, counter_4_q;

  Counter #(.width(4), .max('h9)) counter_1 (
    .Q(counter_1_q), .carry(counter_1_carry), .clk(CLK), .clr(or_1_out));  // open: load, D, count
  or or_1 (or_1_out, counter_1_carry, RESET, t_ff_1_q);
  Adder #(.width(4)) adder_1 (.a(4'b0001), .b(counter_1_q), .out(adder_1_out));  // open: cin, cout
  or or_2 (or_2_out, and_1_out, counter_4_carry, counter_1_carry);
  T_Flip_Flop t_ff_1 (.clk(or_2_out), .T(1'b1), .Q(t_ff_1_q), .Qn(t_ff_1_qn));  // open: preset, reset, en
  // Probe on OUTPUT_1
  Counter #(.width(4), .max('h1)) counter_2 (
    .Q(OUTPUT_1), .clk(counter_1_carry), .clr(counter_4_carry));  // open: load, D, count, carry
  and and_1 (and_1_out, t_ff_1_q, RESET);
  or or_3 (or_3_out, counter_4_carry, RESET, t_ff_1_qn);
  // Probe on OUTPUT_0
  Multiplexer #(.width(4), .enable("false")) multiplexer_1 (
    .in0(adder_1_out), .in1(counter_4_q), .out(OUTPUT_0), .sel(t_ff_1_q));
  Counter #(.width(4), .max('h2)) counter_3 (
    .carry(CARRY), .clk(counter_4_carry), .clr(CARRY));  // open: load, D, count, Q
  Counter #(.width(4), .max('h3)) counter_4 (
    .Q(counter_4_q), .carry(counter_4_carry), .clk(CLK), .clr(or_3_out));  // open: load, D, count
  T_Flip_Flop t_ff_2 (.clk(CARRY), .T(1'b1), .Qn(PERIOD));  // open: Q, preset, reset, en
endmodule

module hours_24 (
  input  CLK,
  output [3:0] digit__1,
  output [3:0] digit__0,
  output carry
);

  wire counter_1_carry, or_1_out, t_ff_1_q, t_ff_1_qn;
  wire [3:0] counter_1_q, counter_2_q;

  Counter #(.width(4), .max('h9)) counter_1 (
    .count(t_ff_1_qn), .Q(counter_1_q), .carry(counter_1_carry), .clk(CLK));  // open: load, D, clr
  Multiplexer #(.width(4), .enable("false")) multiplexer_1 (
    .in0(counter_1_q), .in1(counter_2_q), .out(digit__0), .sel(t_ff_1_q));
  Multiplexer #(.width(4), .enable("false")) multiplexer_2 (
    .in0(4'b0000), .in1(4'b0001), .out(digit__1), .sel(t_ff_1_q));
  T_Flip_Flop t_ff_1 (.clk(CLK), .T(or_1_out), .Q(t_ff_1_q), .Qn(t_ff_1_qn));  // open: preset, reset, en
  or or_1 (or_1_out, counter_1_carry, carry);
  Counter #(.width(4), .max('h2)) counter_2 (
    .count(t_ff_1_q), .Q(counter_2_q), .carry(carry), .clk(CLK));  // open: load, D, clr
  Hex_Digit_Display hex_digit_display_1 (.value(digit__0));  // open: dp
  Hex_Digit_Display hex_digit_display_2 (.value(digit__1));  // open: dp

  // Notes on the sheet:
  //   TODO: 24 hour time goes to 24 not 12
endmodule

module months (
  input  CLK,
  input  RESET,
  output [3:0] OUTPUT_1,
  output [3:0] OUTPUT_0,
  output a,
  output b,
  output CARRY
);

  wire and_1_out, counter_1_carry, or_1_out, or_2_out, or_3_out, t_ff_1_q, t_ff_1_qn;
  wire [3:0] adder_1_out, counter_1_q, counter_3_q;

  Counter #(.width(4), .max('h9)) counter_1 (
    .Q(counter_1_q), .carry(counter_1_carry), .clk(CLK), .clr(or_1_out));  // open: load, D, count
  or or_1 (or_1_out, counter_1_carry, RESET, t_ff_1_q);
  Adder #(.width(4)) adder_1 (.a(4'b0001), .b(counter_1_q), .out(adder_1_out));  // open: cin, cout
  or or_2 (or_2_out, and_1_out, CARRY, counter_1_carry);
  T_Flip_Flop t_ff_1 (.clk(or_2_out), .T(1'b1), .Q(t_ff_1_q), .Qn(t_ff_1_qn));  // open: preset, reset, en
  // Probe on OUTPUT_1
  // Probe on OUTPUT_0
  Counter #(.width(4), .max('h1)) counter_2 (
    .Q(OUTPUT_1), .clk(counter_1_carry), .clr(CARRY));  // open: load, D, count, carry
  or or_3 (or_3_out, CARRY, RESET, t_ff_1_qn);
  and and_1 (and_1_out, t_ff_1_q, RESET);
  to_days to_days_1 (.a(OUTPUT_0), .b(OUTPUT_1), .A_2(a), .B_2(b));
  Multiplexer #(.width(4), .enable("false")) multiplexer_1 (
    .in0(adder_1_out), .in1(counter_3_q), .out(OUTPUT_0), .sel(t_ff_1_q));
  Counter #(.width(4), .max('h3)) counter_3 (
    .Q(counter_3_q), .carry(CARRY), .clk(CLK), .clr(or_3_out));  // open: load, D, count
endmodule

module days (
  input  CLK,
  input  A,
  input  B,
  output [3:0] OUTPUT_1,
  output [3:0] OUTPUT_0,
  output CARRY
);

  wire n1_0_1_carry, n1_9_0_9_1_carry, n3_2_1_carry, n8_9_1_carry, not_1_out, or_2_out, or_3_out;
  wire [3:0] multiplexer_1_out, n1_0_1_output, n1_9_0_9_1_output, n8_9_1_output;

  _1_9_0_9 u_1_9_0_9_1 (.RESET(CARRY), .CLK(CLK), .CARRY(n1_9_0_9_1_carry), .OUTPUT(n1_9_0_9_1_output));
  // Probe on OUTPUT_1
  // Probe on OUTPUT_0
  _3_2 u_3_2_1 (.CLK(n1_9_0_9_1_carry), .RESET(CARRY), ._3_2(A), .CARRY(n3_2_1_carry), .OUTPUT(OUTPUT_1));
  assign OUTPUT_0 = n1_9_0_9_1_output | multiplexer_1_out;  // OR_Gate or_1, 4 bits wide
  Multiplexer #(.width(4), .enable("false")) multiplexer_1 (
    .in0(n1_0_1_output), .in1(n8_9_1_output), .out(multiplexer_1_out), .sel(A));
  _1_0 u_1_0_1 (.CLK(CLK), .RESET(or_2_out), ._1_0(B), .CARRY(n1_0_1_carry), .OUTPUT(n1_0_1_output));
  or or_2 (or_2_out, n3_2_1_carry, A);
  not not_1 (not_1_out, A);
  _8_9 u_8_9_1 (.CLK(CLK), .RESET(or_3_out), ._8_9(B), .CARRY(n8_9_1_carry), .OUTPUT(n8_9_1_output));
  or or_3 (or_3_out, n3_2_1_carry, not_1_out);
  or or_4 (CARRY, n8_9_1_carry, n1_0_1_carry);
endmodule

module _1_9_0_9 (
  input  CLK,
  input  RESET,
  output [3:0] OUTPUT,
  output CARRY
);

  wire _0_9_carry, _1_9_carry, or_1_out, or_2_out, or_3_out, t_ff_1_q, t_ff_1_qn;
  wire [3:0] _0_9_q, _1_9_q, adder_1_out;

  Counter #(.width(4), .max('h9)) _1_9 (
    .Q(_1_9_q), .carry(_1_9_carry), .clk(CLK), .clr(or_2_out));  // open: load, D, count
  or or_1 (or_1_out, _1_9_carry, RESET);
  or or_2 (or_2_out, RESET, t_ff_1_q, _1_9_carry);
  Adder #(.width(4)) adder_1 (.a(4'b0001), .b(_1_9_q), .out(adder_1_out));  // open: cin, cout
  or or_3 (or_3_out, RESET, t_ff_1_qn, _0_9_carry);
  T_Flip_Flop t_ff_1 (.clk(or_1_out), .T(1'b1), .Q(t_ff_1_q), .Qn(t_ff_1_qn));  // open: preset, reset, en
  // Probe on OUTPUT
  Multiplexer #(.width(4), .enable("false")) multiplexer_1 (
    .in0(adder_1_out), .in1(_0_9_q), .out(OUTPUT), .sel(t_ff_1_q));
  Counter #(.width(4), .max('ha)) _0_9 (
    .Q(_0_9_q), .carry(_0_9_carry), .clk(CLK), .clr(or_3_out));  // open: load, D, count
  or or_4 (CARRY, _0_9_carry, _1_9_carry);
endmodule

module _3_2 (
  input  CLK,
  input  RESET,
  input  _3_2,
  output [3:0] OUTPUT,
  output CARRY
);

  wire _2_carry, _3_carry, not_1_out, or_1_out, or_2_out;
  wire [3:0] _2_q, _3_q;

  // Probe on OUTPUT
  Counter #(.width(4), .max('h3)) _3 (.Q(_3_q), .carry(_3_carry), .clk(CLK), .clr(or_1_out));  // open: load, D, count
  or or_1 (or_1_out, RESET, _3_2);
  Multiplexer #(.width(4), .enable("false")) multiplexer_1 (.in0(_3_q), .in1(_2_q), .out(OUTPUT), .sel(_3_2));
  Counter #(.width(4), .max('h2)) _2 (.Q(_2_q), .carry(_2_carry), .clk(CLK), .clr(or_2_out));  // open: load, D, count
  or or_2 (or_2_out, RESET, not_1_out);
  not not_1 (not_1_out, _3_2);
  nor nor_1 (CARRY, _2_carry, _3_carry);
endmodule

module _1_0 (
  input  CLK,
  input  RESET,
  input  _1_0,
  output [3:0] OUTPUT,
  output CARRY
);

  wire _0_carry, _1_carry, not_1_out, or_1_out, or_2_out;
  wire [3:0] _0_q, _1_q;

  // Probe on OUTPUT
  Counter #(.width(4), .max('h2)) _1 (.Q(_1_q), .carry(_1_carry), .clk(CLK), .clr(or_1_out));  // open: load, D, count
  or or_1 (or_1_out, RESET, _1_carry, _1_0);
  Multiplexer #(.width(4), .enable("false")) multiplexer_1 (.in0(_1_q), .in1(_0_q), .out(OUTPUT), .sel(_1_0));
  Counter #(.width(4), .max('h1)) _0 (.Q(_0_q), .carry(_0_carry), .clk(CLK), .clr(or_2_out));  // open: load, D, count
  or or_2 (or_2_out, RESET, _0_carry, not_1_out);
  not not_1 (not_1_out, _1_0);
  or or_3 (CARRY, _0_carry, _1_carry);
endmodule

module _8_9 (
  input  CLK,
  input  RESET,
  input  _8_9,
  output [3:0] OUTPUT,
  output CARRY
);

  wire _8_carry, _9_carry, not_1_out, or_1_out, or_2_out;
  wire [3:0] _8_q, _9_q;

  // Probe on OUTPUT
  Counter #(.width(4), .max('h9)) _8 (.Q(_8_q), .carry(_8_carry), .clk(CLK), .clr(or_1_out));  // open: load, D, count
  or or_1 (or_1_out, RESET, _8_carry, _8_9);
  Multiplexer #(.width(4), .enable("false")) multiplexer_1 (.in0(_8_q), .in1(_9_q), .out(OUTPUT), .sel(_8_9));
  Counter #(.width(4), .max('ha)) _9 (.Q(_9_q), .carry(_9_carry), .clk(CLK), .clr(or_2_out));  // open: load, D, count
  or or_2 (or_2_out, RESET, _9_carry, not_1_out);
  not not_1 (not_1_out, _8_9);
  or or_3 (CARRY, _9_carry, _8_carry);
endmodule

module to_days (
  input  [3:0] a,
  input  [3:0] b,
  output A_2,
  output B_2
);

  wire and_2_out, and_3_out, and_4_out;

  and and_1 (A_2, ~b[2], b[1], ~b[0]);  // AND_Gate
  and and_2 (and_2_out, b[2], ~b[0]);  // AND_Gate
  and and_3 (and_3_out, b[3], b[0]);
  and and_4 (and_4_out, a[1], ~a[0]);  // AND_Gate
  or or_1 (B_2, and_2_out, and_3_out, and_4_out);
endmodule

module years (
  input  CLK,
  output [3:0] OUTPUT_2,
  output [3:0] OUTPUT_3,
  output [3:0] OUTPUT_1,
  output [3:0] OUTPUT_0,
  output CARRY
);

  wire counter_1_carry, counter_2_carry, counter_3_carry;
  wire [3:0] counter_4_q;

  Counter #(.width(4), .max('ha)) counter_1 (
    .Q(OUTPUT_0), .carry(counter_1_carry), .clk(CLK), .clr(counter_1_carry));  // open: load, D, count
  Counter #(.width(4), .max('ha)) counter_2 (
    .Q(OUTPUT_2), .carry(counter_2_carry), .clk(counter_3_carry), .clr(counter_2_carry));  // open: load, D, count
  Counter #(.width(4), .max('ha)) counter_3 (
    .Q(OUTPUT_1), .carry(counter_3_carry), .clk(counter_1_carry), .clr(counter_3_carry));  // open: load, D, count
  Counter #(.width(4), .max('h8)) counter_4 (
    .Q(counter_4_q), .carry(CARRY), .clk(counter_2_carry), .clr(CARRY));  // open: load, D, count
  Adder #(.width(4)) adder_1 (.a(4'b0010), .b(counter_4_q), .out(OUTPUT_3));  // open: cin, cout
endmodule
